// Logisim project byte_enable_gen.circ as structural Verilog: 1 circuit, main circuit byte_enable_gen
module byte_enable_gen (
  input  [31:0] INSTRUCTION,
  input  MemRW,
  output [3:0] WRITE_ENABLE
);

  wire comparator_1_eq, comparator_2_eq, comparator_3_eq, comparator_4_eq, is_sb_out, is_sh_out;
  wire [3:0] multiplexer_1_out, multiplexer_2_out;

  Comparator #(.width(7)) comparator_1 (.a(INSTRUCTION[6:0]), .b(7'b0100011), .eq(comparator_1_eq));  // open: gt, lt
  Comparator #(.width(3)) comparator_2 (.a(INSTRUCTION[14:12]), .b(3'b001), .eq(comparator_2_eq));  // open: gt, lt
  and is_sh (is_sh_out, comparator_1_eq, comparator_2_eq);
  Comparator #(.width(7)) comparator_3 (.a(INSTRUCTION[6:0]), .b(7'b0100011), .eq(comparator_3_eq));  // open: gt, lt
  Comparator #(.width(3)) comparator_4 (.a(INSTRUCTION[14:12]), .b(3'b000), .eq(comparator_4_eq));  // open: gt, lt
  Multiplexer #(.enable("false"), .width(4)) multiplexer_1 (
    .in0(4'b1111), .in1(4'b0011), .out(multiplexer_1_out), .sel(is_sh_out));
  and is_sb (is_sb_out, comparator_3_eq, comparator_4_eq);
  Multiplexer #(.enable("false"), .width(4)) multiplexer_2 (
    .in0(multiplexer_1_out), .in1(4'b0001), .out(multiplexer_2_out), .sel(is_sb_out));
  Multiplexer #(.enable("false"), .width(4)) multiplexer_3 (
    .in0(4'b0000), .in1(multiplexer_2_out), .out(WRITE_ENABLE), .sel(MemRW));

  // Other names for the same wires on the sheet: opcode[6:0] = INSTRUCTION[6:0]; funct3[2:0] = INSTRUCTION[14:12];
  //   funct7[6:0] = INSTRUCTION[31:25]
endmodule
