// Logisim project cpu.circ as structural Verilog: 1 circuit, main circuit cpu
module cpu (
  input  clk,
  input  [31:0] INSTRUCTION,
  input  [31:0] READ_DATA,
  output [31:0] WRITE_ADDRESS,
  output [31:0] PROGRAM_COUNTER,
  output [31:0] ra,
  output [31:0] sp,
  output [31:0] t0,
  output [31:0] t1,
  output [31:0] t2,
  output [31:0] s0,
  output [31:0] s1,
  output [31:0] a0,
  output [31:0] tohost,
  output [3:0] WRITE_ENABLE,
  output [31:0] WRITE_DATA
);

  wire branch_comp_1_breq, branch_comp_1_brlt, comparator_1_eq, comparator_2_eq, comparator_3_eq,
       comparator_4_eq, control_logic_1_asel, control_logic_1_brun, control_logic_1_bsel,
       control_logic_1_csrsel, control_logic_1_csrwen, control_logic_1_memrw, control_logic_1_pcsel,
       control_logic_1_regwen, is_lh_out, is_lw_out;
  wire [1:0] control_logic_1_wbsel;
  wire [2:0] control_logic_1_immsel, funct3;
  wire [3:0] control_logic_1_alusel;
  wire [4:0] register_1_q;
  wire [6:0] funct7, opcode;
  wire [9:0] register_1_q_2;
  wire [31:0] adder_1_out, adder_2_out, bit_extender_1_out, bit_extender_2_out, imm_gen_1_imm,
       multiplexer_1_out, multiplexer_2_out, multiplexer_3_out, multiplexer_4_out, multiplexer_5_out,
       multiplexer_6_out, multiplexer_7_out, READ_DATA2, regfile_1_read_data_1, register_2_q;

  Adder #(.width(32)) adder_1 (.a(PROGRAM_COUNTER), .b(32'h4), .out(adder_1_out));  // open: cin, cout
  Register #(.width(32)) PC (.D(multiplexer_1_out), .clk(clk), .Q(PROGRAM_COUNTER));  // open: en, clr
  Multiplexer #(.enable("false"), .width(32)) multiplexer_1 (
    .in0(adder_1_out), .in1(WRITE_ADDRESS), .out(multiplexer_1_out), .sel(control_logic_1_pcsel));
  Register #(.width(32)) register_1 (
    .D(multiplexer_2_out), .clk(clk), .Q({funct7, register_1_q_2, funct3, register_1_q, opcode}));  // open: en, clr
  Multiplexer #(.enable("false"), .width(32)) multiplexer_2 (
    .in0(INSTRUCTION), .in1(32'h13), .out(multiplexer_2_out), .sel(control_logic_1_pcsel));
  Register #(.width(32)) register_2 (.D(PROGRAM_COUNTER), .clk(clk), .Q(register_2_q));  // open: en, clr
  control_logic control_logic_1 (
    .CSRWen(control_logic_1_csrwen), .PCSel(control_logic_1_pcsel), .RegWEn(control_logic_1_regwen),
    .ImmSel(control_logic_1_immsel), .BrUn(control_logic_1_brun), .ASel(control_logic_1_asel),
    .BSel(control_logic_1_bsel), .ALUSel(control_logic_1_alusel), .MemRW(control_logic_1_memrw),
    .WBSel(control_logic_1_wbsel), .CSRSel(control_logic_1_csrsel),
    .inst({funct7, register_1_q_2, funct3, register_1_q, opcode}), .BrEq(branch_comp_1_breq),
    .BrLt(branch_comp_1_brlt));
  imm_gen imm_gen_1 (
    .inst({funct7, register_1_q_2, funct3, register_1_q, opcode}), .ImmSel(control_logic_1_immsel),
    .imm(imm_gen_1_imm));
  regfile regfile_1 (
    .rs1(register_1_q_2[4:0]), .rs2(register_1_q_2[9:5]), .rd(register_1_q), .Write_Data(multiplexer_6_out),
    .RegWEn(control_logic_1_regwen), .clk(clk), .ra(ra), .sp(sp), .t0(t0), .t1(t1), .t2(t2), .s0(s0),
    .s1(s1), .a0(a0), .Read_Data_1(regfile_1_read_data_1), .Read_Data_2(WRITE_DATA));
  branch_comp branch_comp_1 (
    .rs1(regfile_1_read_data_1), .rs2(WRITE_DATA), .BrUn(control_logic_1_brun), .BrEq(branch_comp_1_breq),
    .BrLt(branch_comp_1_brlt));
  Multiplexer #(.enable("false"), .width(32)) multiplexer_3 (
    .in0(imm_gen_1_imm), .in1(regfile_1_read_data_1), .out(multiplexer_3_out), .sel(control_logic_1_csrsel));
  Adder #(.width(32)) adder_2 (.a(32'h4), .b(register_2_q), .out(adder_2_out));  // open: cin, cout
  Multiplexer #(.enable("false"), .width(32)) multiplexer_4 (
    .in0(regfile_1_read_data_1), .in1(register_2_q), .out(multiplexer_4_out), .sel(control_logic_1_asel));
  Multiplexer #(.enable("false"), .width(32)) multiplexer_5 (
    .in0(WRITE_DATA), .in1(imm_gen_1_imm), .out(multiplexer_5_out), .sel(control_logic_1_bsel));
  alu alu_1 (.Result(WRITE_ADDRESS), .A(multiplexer_4_out), .B(multiplexer_5_out), .ALUSel(control_logic_1_alusel));
  csr csr_1 (
    .CSR_address(12'h51e), .CSR_din(multiplexer_3_out), .CSR_WE(control_logic_1_csrwen), .clk(clk),
    .tohost(tohost));
  // byte_enable_gen byte_enable_gen_1: pin names not known; wires that end beside it: {funct7, register_1_q_2, funct3, register_1_q, opcode}, control_logic_1_memrw, WRITE_ENABLE
  Multiplexer #(.enable("false"), .select(2), .width(32)) multiplexer_6 (
    .in0(READ_DATA2), .in1(WRITE_ADDRESS), .in2(adder_2_out), .in3(imm_gen_1_imm), .out(multiplexer_6_out),
    .sel(control_logic_1_wbsel));
  assign bit_extender_1_out = {{24{READ_DATA[7]}}, READ_DATA[7:0]};  // Bit_Extender bit_extender_1
  assign bit_extender_2_out = {{16{READ_DATA[15]}}, READ_DATA[15:0]};  // Bit_Extender bit_extender_2
  Comparator #(.width(7)) comparator_1 (.a(opcode), .b(7'b0000011), .eq(comparator_1_eq));  // open: gt, lt
  and is_lh (is_lh_out, comparator_1_eq, comparator_2_eq);
  Comparator #(.width(3)) comparator_2 (.a(funct3), .b(3'b001), .eq(comparator_2_eq));  // open: gt, lt
  Multiplexer #(.enable("false"), .width(32)) multiplexer_7 (
    .in0(bit_extender_1_out), .in1(bit_extender_2_out), .out(multiplexer_7_out), .sel(is_lh_out));
  Comparator #(.width(7)) comparator_3 (.a(opcode), .b(7'b0000011), .eq(comparator_3_eq));  // open: gt, lt
  Comparator #(.width(3)) comparator_4 (.a(funct3), .b(3'b010), .eq(comparator_4_eq));  // open: gt, lt
  Multiplexer #(.enable("false"), .width(32)) multiplexer_8 (
    .in0(multiplexer_7_out), .in1(READ_DATA), .out(READ_DATA2), .sel(is_lw_out));
  and is_lw (is_lw_out, comparator_3_eq, comparator_4_eq);

  // Notes on the sheet:
  //   Output to IMEM
  //   IMEM (do **NOT** move this)
  //   Inputs from IMEM
  //   It is OK to move the PC, RegFile, ALU, MEM, Branch Comp, Imm Gen, and Control Logic to wherever is most convenient for you when constructing your CPU, and to delete this text
  //   Inputs/Outputs for testing. Do **NOT** move these.
  //   Outputs To DMEM
  //   DMEM (do **NOT** move this)
  //   Inputs From DMEM
endmodule
