// Logisim project my_control_logic.circ as structural Verilog: 1 circuit, main circuit control_logic
module control_logic (
  input  [31:0] inst,
  input  BrEq,
  input  BrLt,
  output PCSel,
  output RegWEn,
  output [2:0] ImmSel,
  output BrUn,
  output ASel,
  output BSel,
  output [3:0] ALUSel,
  output MemRW,
  output [1:0] WBSel,
  output CSRSel,
  output CSRWen
);

  wire comparator_2_eq, comparator_3_eq, comparator_4_eq, comparator_5_eq, comparator_6_eq, comparator_11_eq,
       comparator_14_eq, comparator_16_eq, comparator_17_eq, comparator_18_eq, comparator_19_eq, is_I, is_R,
       is_S, is_SB, is_U, is_UJ, not_1_out, not_2_out, not_3_out, or_2_out, or_4_out;
  wire [1:0] multiplexer_12_out;
  wire [2:0] multiplexer_5_out, multiplexer_6_out, multiplexer_7_out;
  wire [3:0] multiplexer_2_out, multiplexer_3_out, multiplexer_4_out, multiplexer_8_out, multiplexer_10_out;

  not not_1 (not_1_out, BrLt);
  not not_2 (not_2_out, BrEq);
  Multiplexer #(.enable("false"), .select(3)) multiplexer_1 (
    .in0(BrEq), .in1(not_2_out), .in4(BrLt), .in5(not_3_out), .in6(BrLt), .in7(not_1_out), .out(PCSel),
    .sel(inst[14:12]));  // open: in2, in3
  not not_3 (not_3_out, BrLt);
  Multiplexer #(.enable("false"), .select(3), .width(4)) multiplexer_2 (
    .in0(4'b0000), .in1(4'b0110), .in2(4'b0111), .in4(4'b0011), .in5(4'b0100), .in6(4'b0010), .in7(4'b0001),
    .out(multiplexer_2_out), .sel(inst[14:12]));  // open: in3
  Multiplexer #(.enable("false"), .select(2), .width(4)) multiplexer_3 (
    .in0(4'b1010), .in1(4'b1110), .in3(4'b1011), .out(multiplexer_3_out), .sel(inst[13:12]));  // open: in2
  Multiplexer #(.enable("false"), .select(3), .width(4)) multiplexer_4 (
    .in0(4'b1100), .in5(4'b0101), .out(multiplexer_4_out), .sel(inst[14:12]));  // open: in1, in2, in3, in4, in6, in7
  or or_1 (RegWEn, is_R, is_I, is_U, is_UJ);
  or or_2 (or_2_out, is_U, is_UJ);
  Multiplexer #(.enable("false"), .width(3)) multiplexer_5 (
    .in0(multiplexer_6_out), .in1(3'b011), .out(multiplexer_5_out), .sel(is_SB));
  Multiplexer #(.enable("false"), .width(3)) multiplexer_6 (
    .in0(multiplexer_7_out), .in1(3'b010), .out(multiplexer_6_out), .sel(is_S));
  Multiplexer #(.enable("false"), .width(3)) multiplexer_7 (
    .in0(3'b000), .in1(3'b001), .out(multiplexer_7_out), .sel(is_I));
  Multiplexer #(.enable("false"), .select(2), .width(4)) multiplexer_8 (
    .in0(multiplexer_2_out), .in1(multiplexer_3_out), .in2(multiplexer_4_out), .out(multiplexer_8_out),
    .sel(inst[26:25]));  // open: in3
  or or_3 (ASel, is_U, is_SB);
  Comparator #(.mode("unsigned"), .width(3)) comparator_1 (.a(inst[14:12]), .b(3'b101), .gt(BrUn));  // open: eq, lt
  Multiplexer #(.enable("false"), .width(3)) multiplexer_9 (
    .in0(multiplexer_5_out), .in1(3'b100), .out(ImmSel), .sel(or_2_out));
  Multiplexer #(.enable("false"), .width(4)) multiplexer_10 (
    .in1(multiplexer_8_out), .out(multiplexer_10_out), .sel(comparator_2_eq));  // open: in0
  Comparator #(.width(7)) comparator_2 (.a(7'b0110011), .b(inst[6:0]), .eq(comparator_2_eq));  // open: gt, lt
  not not_4 (BSel, is_R);
  Comparator #(.width(7)) comparator_3 (.a(7'b0110111), .b(inst[6:0]), .eq(comparator_3_eq));  // open: gt, lt
  Multiplexer #(.enable("false"), .width(4)) multiplexer_11 (
    .in0(multiplexer_10_out), .in1(4'b1101), .out(ALUSel), .sel(comparator_3_eq));
  Multiplexer #(.enable("false"), .width(2)) multiplexer_12 (
    .in0(2'b00), .in1(2'b10), .out(multiplexer_12_out), .sel(comparator_4_eq));
  Comparator #(.mode("unsigned"), .width(7)) comparator_4 (
    .a(7'b0000011), .b(inst[6:0]), .eq(comparator_4_eq));  // open: gt, lt
  Comparator #(.mode("unsigned"), .width(7)) comparator_5 (
    .a(7'b1101111), .b(inst[6:0]), .eq(comparator_5_eq));  // open: gt, lt
  or or_4 (or_4_out, comparator_5_eq, comparator_6_eq);
  Comparator #(.mode("unsigned"), .width(7)) comparator_6 (
    .a(7'b1100111), .b(inst[6:0]), .eq(comparator_6_eq));  // open: gt, lt
  Comparator #(.width(7)) comparator_7 (.a(7'b0100011), .b(inst[6:0]), .eq(MemRW));  // open: gt, lt
  Multiplexer #(.enable("false"), .width(2)) multiplexer_13 (
    .in0(multiplexer_12_out), .in1(2'b01), .out(WBSel), .sel(or_4_out));
  Comparator #(.mode("unsigned"), .width(3)) comparator_8 (.a(3'b001), .b(inst[14:12]), .eq(CSRSel));  // open: gt, lt
  Comparator #(.mode("unsigned"), .width(7)) comparator_9 (.a(inst[6:0]), .b(7'b1110011), .eq(CSRWen));  // open: gt, lt
  Comparator #(.width(7)) comparator_10 (.a(inst[6:0]), .b(7'b0110011), .eq(is_R));  // open: gt, lt
  Comparator #(.width(7)) comparator_11 (.a(inst[6:0]), .b(7'b0000011), .eq(comparator_11_eq));  // open: gt, lt
  Comparator #(.width(7)) comparator_12 (.a(inst[6:0]), .b(7'b0100011), .eq(is_S));  // open: gt, lt
  Comparator #(.width(7)) comparator_13 (.a(inst[6:0]), .b(7'b1100011), .eq(is_SB));  // open: gt, lt
  Comparator #(.width(7)) comparator_14 (.a(inst[6:0]), .b(7'b0010111), .eq(comparator_14_eq));  // open: gt, lt
  Comparator #(.width(7)) comparator_15 (.a(inst[6:0]), .b(7'b1101111), .eq(is_UJ));  // open: gt, lt
  Comparator #(.width(7)) comparator_16 (.a(inst[6:0]), .b(7'b0010011), .eq(comparator_16_eq));  // open: gt, lt
  Comparator #(.width(7)) comparator_17 (.a(inst[6:0]), .b(7'b1100111), .eq(comparator_17_eq));  // open: gt, lt
  Comparator #(.width(7)) comparator_18 (.a(inst[6:0]), .b(7'b1110011), .eq(comparator_18_eq));  // open: gt, lt
  Comparator #(.width(7)) comparator_19 (.a(inst[6:0]), .b(7'b0110111), .eq(comparator_19_eq));  // open: gt, lt
  or or_5 (is_I, comparator_11_eq, comparator_16_eq, comparator_17_eq, comparator_18_eq);
  or or_6 (is_U, comparator_14_eq, comparator_19_eq);

  // Other names for the same wires on the sheet: opcode[6:0] = inst[6:0]; funct3[2:0] = inst[14:12];
  //   funct7[6:0] = inst[31:25]

  // Notes on the sheet:
  //   INPUTS to your circuit
  //   DON'T CHANGE THE LOCATIONS OF THE INPUTS AND OUTPUTS!
  //   OUTPUT from your circuit
endmodule
